// Logisim project casa_de_bilete(logisim).circ as structural Verilog: 7 circuits, main circuit MAIN
module doubledabble (
  input  in_1,
  input  in_2,
  input  in_3,
  input  in_4,
  output out_5,
  output out_6,
  output out_7,
  output out_8
);

  wire decoder_1_out0, decoder_1_out1, decoder_1_out2, decoder_1_out3, decoder_1_out4, decoder_1_out5,
       decoder_1_out6, decoder_1_out7, decoder_1_out8, decoder_1_out9, decoder_1_out15, nor_1_out, or_1_out,
       or_2_out;
  wire [3:0] adder_1_out, multiplexer_1_out;

  Decoder #(.select(4), .enable("false")) decoder_1 (
    .out0(decoder_1_out0), .out1(decoder_1_out1), .out2(decoder_1_out2), .out3(decoder_1_out3),
    .out4(decoder_1_out4), .out5(decoder_1_out5), .out6(decoder_1_out6), .out7(decoder_1_out7),
    .out8(decoder_1_out8), .out9(decoder_1_out9), .out15(decoder_1_out15), .sel({in_4, in_3, in_2, in_1}));  // open: out10, out11, out12, out13, out14
  or or_1 (or_1_out, decoder_1_out0, decoder_1_out1, decoder_1_out2, decoder_1_out3, decoder_1_out4);
  or or_2 (or_2_out, decoder_1_out5, decoder_1_out6, decoder_1_out7, decoder_1_out8, decoder_1_out9);
  Adder #(.width(4)) adder_1 (.a({in_4, in_3, in_2, in_1}), .b(4'b0011), .out(adder_1_out));  // open: cin, cout
  nor nor_1 (nor_1_out, or_2_out, or_1_out);
  Multiplexer #(.width(4), .enable("false")) multiplexer_1 (
    .in0({in_4, in_3, in_2, in_1}), .in1(adder_1_out), .out(multiplexer_1_out), .sel(or_2_out));
  Multiplexer #(.width(4), .enable("false")) multiplexer_2 (
    .in0(multiplexer_1_out), .in1(4'b0000), .out({out_8, out_7, out_6, out_5}), .sel(nor_1_out));
endmodule

module doubledabble8biti (
  input  [7:0] in_1,
  output [3:0] out_2,
  output [3:0] out_3,
  output [3:0] out_4
);

  wire doubledabble_1_out_5, doubledabble_1_out_6, doubledabble_1_out_7, doubledabble_1_out_8,
       doubledabble_2_out_5, doubledabble_2_out_6, doubledabble_2_out_7, doubledabble_2_out_8,
       doubledabble_3_out_5, doubledabble_3_out_6, doubledabble_3_out_7, doubledabble_3_out_8,
       doubledabble_4_out_5, doubledabble_4_out_6, doubledabble_4_out_7, doubledabble_4_out_8,
       doubledabble_5_out_5, doubledabble_5_out_6, doubledabble_5_out_7, doubledabble_5_out_8,
       doubledabble_6_out_5, doubledabble_6_out_6, doubledabble_6_out_7, doubledabble_6_out_8,
       doubledabble_7_out_5, doubledabble_7_out_6, doubledabble_7_out_7, doubledabble_8_out_5,
       doubledabble_8_out_6, doubledabble_8_out_7, doubledabble_10_out_5, doubledabble_10_out_6,
       doubledabble_10_out_7, doubledabble_10_out_8, doubledabble_12_out_5, doubledabble_12_out_6,
       doubledabble_12_out_7;

  doubledabble doubledabble_1 (
    .in_1(in_1[7]), .in_2(doubledabble_2_out_5), .in_3(doubledabble_2_out_6), .in_4(doubledabble_2_out_7),
    .out_5(doubledabble_1_out_5), .out_6(doubledabble_1_out_6), .out_7(doubledabble_1_out_7),
    .out_8(doubledabble_1_out_8));
  doubledabble doubledabble_2 (
    .in_1(1'b0), .in_2(1'b0), .in_3(1'b0), .in_4(1'b0), .out_5(doubledabble_2_out_5),
    .out_6(doubledabble_2_out_6), .out_7(doubledabble_2_out_7), .out_8(doubledabble_2_out_8));
  doubledabble doubledabble_3 (
    .in_1(in_1[5]), .in_2(doubledabble_4_out_5), .in_3(doubledabble_4_out_6), .in_4(doubledabble_4_out_7),
    .out_5(doubledabble_3_out_5), .out_6(doubledabble_3_out_6), .out_7(doubledabble_3_out_7),
    .out_8(doubledabble_3_out_8));
  doubledabble doubledabble_4 (
    .in_1(in_1[6]), .in_2(doubledabble_1_out_5), .in_3(doubledabble_1_out_6), .in_4(doubledabble_1_out_7),
    .out_5(doubledabble_4_out_5), .out_6(doubledabble_4_out_6), .out_7(doubledabble_4_out_7),
    .out_8(doubledabble_4_out_8));
  doubledabble doubledabble_5 (
    .in_1(in_1[3]), .in_2(doubledabble_6_out_5), .in_3(doubledabble_6_out_6), .in_4(doubledabble_6_out_7),
    .out_5(doubledabble_5_out_5), .out_6(doubledabble_5_out_6), .out_7(doubledabble_5_out_7),
    .out_8(doubledabble_5_out_8));
  doubledabble doubledabble_6 (
    .in_1(in_1[4]), .in_2(doubledabble_3_out_5), .in_3(doubledabble_3_out_6), .in_4(doubledabble_3_out_7),
    .out_5(doubledabble_6_out_5), .out_6(doubledabble_6_out_6), .out_7(doubledabble_6_out_7),
    .out_8(doubledabble_6_out_8));
  doubledabble doubledabble_7 (
    .in_1(doubledabble_6_out_8), .in_2(doubledabble_8_out_5), .in_3(doubledabble_8_out_6),
    .in_4(doubledabble_8_out_7), .out_5(doubledabble_7_out_5), .out_6(doubledabble_7_out_6),
    .out_7(doubledabble_7_out_7), .out_8(out_4[2]));
  doubledabble doubledabble_8 (
    .in_1(doubledabble_3_out_8), .in_2(doubledabble_4_out_8), .in_3(doubledabble_1_out_8),
    .in_4(doubledabble_2_out_8), .out_5(doubledabble_8_out_5), .out_6(doubledabble_8_out_6),
    .out_7(doubledabble_8_out_7), .out_8(out_4[3]));
  doubledabble doubledabble_9 (
    .in_1(in_1[1]), .in_2(doubledabble_10_out_5), .in_3(doubledabble_10_out_6), .in_4(doubledabble_10_out_7),
    .out_5(out_2[1]), .out_6(out_2[2]), .out_7(out_2[3]), .out_8(out_3[0]));
  doubledabble doubledabble_10 (
    .in_1(in_1[2]), .in_2(doubledabble_5_out_5), .in_3(doubledabble_5_out_6), .in_4(doubledabble_5_out_7),
    .out_5(doubledabble_10_out_5), .out_6(doubledabble_10_out_6), .out_7(doubledabble_10_out_7),
    .out_8(doubledabble_10_out_8));
  doubledabble doubledabble_11 (
    .in_1(doubledabble_10_out_8), .in_2(doubledabble_12_out_5), .in_3(doubledabble_12_out_6),
    .in_4(doubledabble_12_out_7), .out_5(out_3[1]), .out_6(out_3[2]), .out_7(out_3[3]), .out_8(out_4[0]));
  doubledabble doubledabble_12 (
    .in_1(doubledabble_5_out_8), .in_2(doubledabble_7_out_5), .in_3(doubledabble_7_out_6),
    .in_4(doubledabble_7_out_7), .out_5(doubledabble_12_out_5), .out_6(doubledabble_12_out_6),
    .out_7(doubledabble_12_out_7), .out_8(out_4[1]));

  assign out_2[0] = in_1[0];
endmodule

module bcdencoder (
  input  [3:0] in_1,
  output G,
  output F,
  output A,
  output B,
  output E,
  output D,
  output C
);

  wire decoder_1_out0, decoder_1_out1, decoder_1_out2, decoder_1_out3, decoder_1_out4, decoder_1_out5,
       decoder_1_out6, decoder_1_out7, decoder_1_out8, decoder_1_out9;

  Decoder #(.select(4), .enable("false")) decoder_1 (
    .out0(decoder_1_out0), .out1(decoder_1_out1), .out2(decoder_1_out2), .out3(decoder_1_out3),
    .out4(decoder_1_out4), .out5(decoder_1_out5), .out6(decoder_1_out6), .out7(decoder_1_out7),
    .out8(decoder_1_out8), .out9(decoder_1_out9), .sel(in_1));  // open: out10, out11, out12, out13, out14, out15
  or u_A (A, decoder_1_out0, decoder_1_out2, decoder_1_out3, decoder_1_out5, decoder_1_out6, decoder_1_out7, decoder_1_out8, decoder_1_out9);
  _7_Segment_Display u_7_segment_display_1 (.g(G), .f(F), .a(A), .b(B), .e(E), .d(D), .c(C));  // open: dp
  or u_B (B, decoder_1_out0, decoder_1_out1, decoder_1_out2, decoder_1_out3, decoder_1_out4, decoder_1_out7, decoder_1_out8, decoder_1_out9);
  or u_C (C, decoder_1_out0, decoder_1_out1, decoder_1_out3, decoder_1_out4, decoder_1_out5, decoder_1_out6, decoder_1_out7, decoder_1_out8, decoder_1_out9);
  or u_D (D, decoder_1_out0, decoder_1_out2, decoder_1_out3, decoder_1_out5, decoder_1_out6, decoder_1_out8);
  or u_E (E, decoder_1_out0, decoder_1_out2, decoder_1_out6, decoder_1_out8);
  or u_F (F, decoder_1_out0, decoder_1_out4, decoder_1_out5, decoder_1_out6, decoder_1_out8, decoder_1_out9);
  or u_G (G, decoder_1_out2, decoder_1_out3, decoder_1_out4, decoder_1_out5, decoder_1_out6, decoder_1_out8, decoder_1_out9);
endmodule

module afisor (
  input  [7:0] in_1,
  output [3:0] out_2,
  output [3:0] out_3,
  output [3:0] out_4
);

  wire bcdencoder_1_a, bcdencoder_1_b, bcdencoder_1_c, bcdencoder_1_d, bcdencoder_1_e, bcdencoder_1_f,
       bcdencoder_1_g, bcdencoder_2_a, bcdencoder_2_b, bcdencoder_2_c, bcdencoder_2_d, bcdencoder_2_e,
       bcdencoder_2_f, bcdencoder_2_g, bcdencoder_3_a, bcdencoder_3_b, bcdencoder_3_c, bcdencoder_3_d,
       bcdencoder_3_e, bcdencoder_3_f, bcdencoder_3_g;

  _7_Segment_Display u_7_segment_display_1 (
    .g(bcdencoder_1_g), .f(bcdencoder_1_f), .a(bcdencoder_1_a), .b(bcdencoder_1_b), .e(bcdencoder_1_e),
    .d(bcdencoder_1_d), .c(bcdencoder_1_c));  // open: dp
  bcdencoder bcdencoder_1 (
    .in_1(out_4), .E(bcdencoder_1_e), .D(bcdencoder_1_d), .C(bcdencoder_1_c), .G(bcdencoder_1_g),
    .F(bcdencoder_1_f), .A(bcdencoder_1_a), .B(bcdencoder_1_b));
  doubledabble8biti doubledabble8biti_1 (.in_1(in_1), .out_2(out_2), .out_3(out_3), .out_4(out_4));
  _7_Segment_Display u_7_segment_display_2 (
    .g(bcdencoder_2_g), .f(bcdencoder_2_f), .a(bcdencoder_2_a), .b(bcdencoder_2_b), .e(bcdencoder_2_e),
    .d(bcdencoder_2_d), .c(bcdencoder_2_c));  // open: dp
  bcdencoder bcdencoder_2 (
    .in_1(out_3), .E(bcdencoder_2_e), .D(bcdencoder_2_d), .C(bcdencoder_2_c), .G(bcdencoder_2_g),
    .F(bcdencoder_2_f), .A(bcdencoder_2_a), .B(bcdencoder_2_b));
  _7_Segment_Display u_7_segment_display_3 (
    .g(bcdencoder_3_g), .f(bcdencoder_3_f), .a(bcdencoder_3_a), .b(bcdencoder_3_b), .e(bcdencoder_3_e),
    .d(bcdencoder_3_d), .c(bcdencoder_3_c));  // open: dp
  bcdencoder bcdencoder_3 (
    .in_1(out_2), .E(bcdencoder_3_e), .D(bcdencoder_3_d), .C(bcdencoder_3_c), .G(bcdencoder_3_g),
    .F(bcdencoder_3_f), .A(bcdencoder_3_a), .B(bcdencoder_3_b));
endmodule

module produs16biti (
  input  [7:0] in_1,
  input  [7:0] in_2,
  output [7:0] out_3,
  output [7:0] out_4
);

  Multiplier #(.width(16)) multiplier_1 (
    .a({{8{1'b0}}, in_1}), .b({{8{1'b0}}, in_2}), .out({out_4, out_3}));  // open: cin, cout
endmodule

module suma16biti (
  input  [7:0] _0_7,
  input  [7:0] _8_15,
  input  [7:0] in_3,
  input  [7:0] in_4,
  input  [7:0] in_5,
  input  [7:0] in_6,
  input  [7:0] in_7,
  input  [7:0] in_8,
  input  [7:0] in_9,
  input  [7:0] in_10,
  input  [7:0] in_11,
  input  [7:0] in_12,
  output [7:0] _0_7_2,
  output [7:0] out_14
);

  wire adder_1_cout, adder_3_cout, adder_5_cout, adder_7_cout, adder_9_cout;
  wire [7:0] adder_1_out, adder_2_out, adder_3_out, adder_4_out, adder_5_out, adder_6_out, adder_7_out,
       adder_8_out, produs16biti_1_out_3, produs16biti_1_out_4, produs16biti_2_out_3, produs16biti_2_out_4,
       produs16biti_3_out_3, produs16biti_3_out_4, produs16biti_4_out_3, produs16biti_4_out_4,
       produs16biti_5_out_3, produs16biti_5_out_4, produs16biti_6_out_3, produs16biti_6_out_4;

  produs16biti produs16biti_1 (.in_1(_0_7), .in_2(_8_15), .out_3(produs16biti_1_out_3), .out_4(produs16biti_1_out_4));
  produs16biti produs16biti_2 (.in_1(in_3), .in_2(in_4), .out_3(produs16biti_2_out_3), .out_4(produs16biti_2_out_4));
  produs16biti produs16biti_3 (.in_1(in_5), .in_2(in_6), .out_3(produs16biti_3_out_3), .out_4(produs16biti_3_out_4));
  produs16biti produs16biti_4 (.in_1(in_7), .in_2(in_8), .out_3(produs16biti_4_out_3), .out_4(produs16biti_4_out_4));
  produs16biti produs16biti_5 (.in_1(in_9), .in_2(in_10), .out_3(produs16biti_5_out_3), .out_4(produs16biti_5_out_4));
  produs16biti produs16biti_6 (.in_1(in_11), .in_2(in_12), .out_3(produs16biti_6_out_3), .out_4(produs16biti_6_out_4));
  Adder adder_1 (
    .a(produs16biti_1_out_3), .b(produs16biti_2_out_3), .out(adder_1_out), .cout(adder_1_cout));  // open: cin
  Adder adder_2 (
    .a(produs16biti_1_out_4), .b(produs16biti_2_out_4), .out(adder_2_out), .cin(adder_1_cout));  // open: cout
  Adder adder_3 (
    .a(produs16biti_3_out_3), .b(produs16biti_4_out_3), .out(adder_3_out), .cout(adder_3_cout));  // open: cin
  Adder adder_4 (
    .a(produs16biti_3_out_4), .b(produs16biti_4_out_4), .out(adder_4_out), .cin(adder_3_cout));  // open: cout
  Adder adder_5 (
    .a(produs16biti_5_out_3), .b(produs16biti_6_out_3), .out(adder_5_out), .cout(adder_5_cout));  // open: cin
  Adder adder_6 (
    .a(produs16biti_5_out_4), .b(produs16biti_6_out_4), .out(adder_6_out), .cin(adder_5_cout));  // open: cout
  Adder adder_7 (.a(adder_1_out), .b(adder_3_out), .out(adder_7_out), .cout(adder_7_cout));  // open: cin
  Adder adder_8 (.a(adder_2_out), .b(adder_4_out), .out(adder_8_out), .cin(adder_7_cout));  // open: cout
  Adder adder_9 (.a(adder_7_out), .b(adder_5_out), .out(_0_7_2), .cout(adder_9_cout));  // open: cin
  Adder adder_10 (.a(adder_8_out), .b(adder_6_out), .out(out_14), .cin(adder_9_cout));  // open: cout

  // Notes on the sheet:
  //   8-15
endmodule

module MAIN (
  input  [7:0] in_1,
  input  [7:0] Suma_platita,
  input  [7:0] in_3,
  input  [7:0] in_4,
  input  [7:0] in_5,
  input  [7:0] in_6,
  input  [7:0] in_7,
  input  CANCEL,
  input  [7:0] in_9,
  input  CONFIRMARE_TRANZACTIE,
  input  [7:0] in_11
);

  wire and_1_out, and_2_out, comparator_1_gt, comparator_2_eq, comparator_2_lt, comparator_3_gt, not_1_out,
       not_2_out, not_3_out, or_1_out, or_2_out;
  wire [3:0] afisor_1_out_2, afisor_1_out_3, afisor_1_out_4, afisor_2_out_2, afisor_2_out_3, afisor_2_out_4,
       afisor_3_out_2, afisor_3_out_3, afisor_3_out_4, afisor_4_out_2, afisor_4_out_3, afisor_4_out_4,
       afisor_5_out_2, afisor_5_out_3, afisor_5_out_4;
  wire [7:0] multiplexer_1_out, subtractor_1_out, suma16biti_1__0_7_2, suma16biti_1_out_14;

  Subtractor subtractor_1 (.a(Suma_platita), .b(in_1), .out(subtractor_1_out));  // open: bin, bout
  suma16biti suma16biti_1 (
    ._0_7(in_3), ._8_15(8'h1), .in_3(in_4), .in_4(8'h2), .in_5(in_5), .in_6(8'h5), .in_7(in_6), .in_8(8'ha),
    .in_9(in_7), .in_10(8'h14), .in_11(in_9), .in_12(8'h32), ._0_7_2(suma16biti_1__0_7_2),
    .out_14(suma16biti_1_out_14));
  Hex_Digit_Display hex_digit_display_1 (.value(afisor_1_out_4));  // open: dp
  afisor afisor_1 (.in_1(in_1), .out_2(afisor_1_out_2), .out_3(afisor_1_out_3), .out_4(afisor_1_out_4));
  Hex_Digit_Display hex_digit_display_2 (.value(afisor_1_out_2));  // open: dp
  Hex_Digit_Display hex_digit_display_3 (.value(afisor_1_out_3));  // open: dp
  afisor afisor_2 (.in_1(Suma_platita), .out_2(afisor_2_out_2), .out_3(afisor_2_out_3), .out_4(afisor_2_out_4));
  Comparator #(.mode("unsigned")) comparator_1 (.a(in_1), .b(Suma_platita), .gt(comparator_1_gt));  // open: eq, lt
  Comparator #(.width(16), .mode("unsigned")) comparator_2 (
    .a({{8{1'b0}}, subtractor_1_out}), .b({suma16biti_1_out_14, suma16biti_1__0_7_2}), .eq(comparator_2_eq),
    .lt(comparator_2_lt));  // open: gt
  Hex_Digit_Display hex_digit_display_4 (.value(afisor_4_out_4));  // open: dp
  Hex_Digit_Display hex_digit_display_5 (.value(afisor_4_out_3));  // open: dp
  afisor afisor_3 (.in_1(suma16biti_1__0_7_2), .out_2(afisor_3_out_2), .out_3(afisor_3_out_3), .out_4(afisor_3_out_4));
  afisor afisor_4 (.in_1(suma16biti_1_out_14), .out_2(afisor_4_out_2), .out_3(afisor_4_out_3), .out_4(afisor_4_out_4));
  Multiplexer #(.width(8), .enable("false")) multiplexer_1 (
    .in0(subtractor_1_out), .in1({8{1'b0}}), .out(multiplexer_1_out), .sel(comparator_1_gt));
  or or_1 (or_1_out, comparator_2_eq, comparator_2_lt);
  Hex_Digit_Display hex_digit_display_6 (.value(afisor_3_out_4));  // open: dp
  Hex_Digit_Display hex_digit_display_7 (.value(afisor_4_out_2), .dp(1'b1));
  Hex_Digit_Display hex_digit_display_8 (.value(afisor_2_out_4));  // open: dp
  Hex_Digit_Display hex_digit_display_9 (.value(afisor_2_out_3));  // open: dp
  not not_1 (not_1_out, CANCEL);
  Comparator #(.mode("unsigned")) comparator_3 (.a(in_11), .b({8{1'b0}}), .gt(comparator_3_gt));  // open: eq, lt
  Hex_Digit_Display hex_digit_display_10 (.value(afisor_3_out_2));  // open: dp
  Hex_Digit_Display hex_digit_display_11 (.value(afisor_3_out_3));  // open: dp
  Hex_Digit_Display hex_digit_display_12 (.value(afisor_2_out_2));  // open: dp
  afisor afisor_5 (.in_1(multiplexer_1_out), .out_2(afisor_5_out_2), .out_3(afisor_5_out_3), .out_4(afisor_5_out_4));
  not not_2 (not_2_out, comparator_1_gt);
  and and_1 (and_1_out, or_1_out, not_1_out, comparator_3_gt);
  Hex_Digit_Display hex_digit_display_13 (.value(afisor_5_out_4));  // open: dp
  Hex_Digit_Display hex_digit_display_14 (.value(afisor_5_out_3));  // open: dp
  not not_3 (not_3_out, and_1_out);
  and and_2 (and_2_out, and_1_out, not_2_out, CONFIRMARE_TRANZACTIE);
  Hex_Digit_Display hex_digit_display_15 (.value(afisor_5_out_2));  // open: dp
  LED led_1 (.in(or_2_out));
  or or_2 (or_2_out, comparator_1_gt, not_3_out);
  LED led_2 (.in(and_2_out));

  // Notes on the sheet:
  //   !
  //   1
  //   2
  //   5
  //   10
  //   20
  //   50
  //   Distanta (in zeci de km)
  //   Numarul de bancnote/monede in casa
  //   a fost folosit hex digit display in loc de 7seg display
  //   pentru a imbunatati aspectul vizual
  //   Componenta care face trecerea de la bcd la 7seg exista
  //   si se numeste "bcdencoder"
  //   PRET
  //   Numar bilete in casa
  //   BANI IN CASA
  //   SUMA PLATITA
  //   REST
  //   Eroare
  //   Eliberare Bilet
endmodule
